# Fritzing sketch Parking Slot (saved by Fritzing 0.9.3b)

parts:
  U1 = NodeMCU V3.0
  Part1 = LCD1602-I2C
  Part2 = RFID-RC522-v2
  Part3 = RFID-RC522-v2

nets:
  N1: U1.D0, Part2.RST, Part3.RST
  N2: U1.D1, Part1.SCL
  N3: U1.D2, Part1.SDA
  N4: U1.D3, Part3.SDA
  N5: U1.D4, Part2.SDA
  3.3V: U1.3V3, Part1.VCC, Part2.3.3V, Part3.3.3V
  GND: U1.GND, Part1.GND, Part2.GND, Part3.GND
  N6: U1.D5, Part2.SCK
  N7: U1.D6, Part2.MOSI
  N8: U1.D7, Part2.MISO

custom parts:
  NodeMCU V3.0: ESP8266 based NodeMCU
  LCD1602-I2C: A standard character display, usually with 2x16 characters. Comes in many colors with LCM1602 IIC attached.
  RFID-RC522-v2: A simple China made RFID-RC522 Reader; do check the pin labels, as this is a MFRC522 based clone.
